// Logisim project Project_Microprocessor_Logisim.circ as structural Verilog
module OR8Bits (
  input  [7:0] Entree1,
  input  [7:0] Entree2,
  output [7:0] SortieOR
);

  or or_1 (SortieOR[0], Entree1[0], Entree2[0]);
  or or_2 (SortieOR[1], Entree1[1], Entree2[1]);
  or or_3 (SortieOR[2], Entree1[2], Entree2[2]);
  or or_4 (SortieOR[3], Entree1[3], Entree2[3]);
  or or_5 (SortieOR[4], Entree1[4], Entree2[4]);
  or or_6 (SortieOR[5], Entree1[5], Entree2[5]);
  or or_7 (SortieOR[6], Entree1[6], Entree2[6]);
  or or_8 (SortieOR[7], Entree1[7], Entree2[7]);
endmodule

module AND8Bits (
  input  [7:0] Entree1,
  input  [7:0] Entree2,
  output [7:0] SortieAND
);

  and and_1 (SortieAND[0], Entree1[0], Entree2[0]);
  and and_2 (SortieAND[1], Entree1[1], Entree2[1]);
  and and_3 (SortieAND[2], Entree1[2], Entree2[2]);
  and and_4 (SortieAND[3], Entree1[3], Entree2[3]);
  and and_5 (SortieAND[4], Entree1[4], Entree2[4]);
  and and_6 (SortieAND[5], Entree1[5], Entree2[5]);
  and and_7 (SortieAND[6], Entree1[6], Entree2[6]);
  and and_8 (SortieAND[7], Entree1[7], Entree2[7]);
endmodule

module XOR8Bits (
  input  [7:0] Entree1,
  input  [7:0] Entree2,
  output [7:0] SortieXOR
);

  xor xor_1 (SortieXOR[0], Entree1[0], Entree2[0]);
  xor xor_2 (SortieXOR[1], Entree1[1], Entree2[1]);
  xor xor_3 (SortieXOR[2], Entree1[2], Entree2[2]);
  xor xor_4 (SortieXOR[3], Entree1[3], Entree2[3]);
  xor xor_5 (SortieXOR[4], Entree1[4], Entree2[4]);
  xor xor_6 (SortieXOR[5], Entree1[5], Entree2[5]);
  xor xor_7 (SortieXOR[6], Entree1[6], Entree2[6]);
  xor xor_8 (SortieXOR[7], Entree1[7], Entree2[7]);
endmodule

module UL (
  input  [7:0] Entree1,
  input  [7:0] Entree2,
  output [7:0] SortieAND,
  output [7:0] SortieOR,
  output [7:0] SortieXOR
);

  AND8Bits and8bits_1 (.Entree1(Entree1), .Entree2(Entree2), .SortieAND(SortieAND));
  OR8Bits or8bits_1 (.Entree1(Entree1), .Entree2(Entree2), .SortieOR(SortieOR));
  XOR8Bits xor8bits_1 (.Entree1(Entree1), .Entree2(Entree2), .SortieXOR(SortieXOR));
endmodule

module Etape2 (
  input  [7:0] Entree1,
  input  [7:0] Entree2,
  output [7:0] SortieAND,
  output [7:0] SortieOR,
  output [7:0] SortieXOR
);

  UL ul_1 (.Entree1(Entree1), .Entree2(Entree2), .SortieAND(SortieAND), .SortieOR(SortieOR), .SortieXOR(SortieXOR));
endmodule

module SommeAdd1Bit (
  input  a,
  input  b,
  input  Rin,
  output Somme
);

  wire and_1_out, and_2_out, and_3_out, and_4_out, and_5_out, and_6_out, not_1_out, not_2_out, not_3_out,
       or_1_out, or_2_out;

  not not_1 (not_1_out, a);
  not not_2 (not_2_out, b);
  not not_3 (not_3_out, Rin);
  and and_1 (and_1_out, not_1_out, b);
  and and_2 (and_2_out, a, not_2_out);
  or or_1 (or_1_out, and_1_out, and_2_out);
  and and_3 (and_3_out, a, b);
  and and_4 (and_4_out, not_1_out, not_2_out);
  or or_2 (or_2_out, and_3_out, and_4_out);
  and and_5 (and_5_out, or_1_out, not_3_out);
  and and_6 (and_6_out, or_2_out, Rin);
  or or_3 (Somme, and_6_out, and_5_out);
endmodule

module RoutAdd1Bit (
  input  a,
  input  b,
  input  Rin,
  output Rout
);

  wire and_1_out, and_2_out, and_3_out, and_4_out, not_1_out, not_2_out, or_1_out;

  not not_1 (not_1_out, a);
  not not_2 (not_2_out, Rin);
  and and_1 (and_1_out, not_1_out, b);
  or or_1 (or_1_out, a, and_1_out);
  and and_2 (and_2_out, or_1_out, Rin);
  and and_3 (and_3_out, a, b);
  and and_4 (and_4_out, and_3_out, not_2_out);
  or or_2 (Rout, and_2_out, and_4_out);
endmodule

module Add1Bit (
  input  a,
  input  b,
  input  Rin,
  output Somme,
  output Rout
);

  SommeAdd1Bit sommeadd1bit_1 (.a(a), .b(b), .Rin(Rin), .Somme(Somme));
  RoutAdd1Bit routadd1bit_1 (.a(a), .b(b), .Rin(Rin), .Rout(Rout));
endmodule

module Add8Bit (
  input  Rin,
  input  [7:0] a,
  input  [7:0] b,
  output [7:0] Somme,
  output Rout
);

  wire add1bit_1_rout, add1bit_2_rout, add1bit_3_rout, add1bit_4_rout, add1bit_5_rout, add1bit_6_rout,
       add1bit_7_rout;

  Add1Bit add1bit_1 (.a(a[0]), .b(b[0]), .Rin(Rin), .Somme(Somme[0]), .Rout(add1bit_1_rout));
  Add1Bit add1bit_2 (.a(a[1]), .b(b[1]), .Rin(add1bit_1_rout), .Somme(Somme[1]), .Rout(add1bit_2_rout));
  Add1Bit add1bit_3 (.a(a[2]), .b(b[2]), .Rin(add1bit_2_rout), .Somme(Somme[2]), .Rout(add1bit_3_rout));
  Add1Bit add1bit_4 (.a(a[3]), .b(b[3]), .Rin(add1bit_3_rout), .Somme(Somme[3]), .Rout(add1bit_4_rout));
  Add1Bit add1bit_5 (.a(a[4]), .b(b[4]), .Rin(add1bit_4_rout), .Somme(Somme[4]), .Rout(add1bit_5_rout));
  Add1Bit add1bit_6 (.a(a[5]), .b(b[5]), .Rin(add1bit_5_rout), .Somme(Somme[5]), .Rout(add1bit_6_rout));
  Add1Bit add1bit_7 (.a(a[6]), .b(b[6]), .Rin(add1bit_6_rout), .Somme(Somme[6]), .Rout(add1bit_7_rout));
  Add1Bit add1bit_8 (.a(a[7]), .b(b[7]), .Rin(add1bit_7_rout), .Somme(Somme[7]), .Rout(Rout));
endmodule

module Etape3 (
  input  Rin,
  input  [7:0] a,
  input  [7:0] b,
  output [7:0] Somme,
  output Rout
);

  Add8Bit add8bit_1 (.Rin(Rin), .a(a), .b(b), .Somme(Somme), .Rout(Rout));
endmodule

module UAL (
  input  Rin,
  input  [7:0] A,
  input  [7:0] B,
  input  [1:0] ChoixOperation,
  output [7:0] Resultat
);

  wire [7:0] add8bit_1_somme, and8bits_1_sortieand, or8bits_1_sortieor, xor8bits_1_sortiexor;

  Add8Bit add8bit_1 (.Rin(Rin), .a(A), .b(B), .Somme(add8bit_1_somme));  // open: Rout
  OR8Bits or8bits_1 (.Entree1(A), .Entree2(B), .SortieOR(or8bits_1_sortieor));
  AND8Bits and8bits_1 (.Entree1(A), .Entree2(B), .SortieAND(and8bits_1_sortieand));
  XOR8Bits xor8bits_1 (.Entree1(A), .Entree2(B), .SortieXOR(xor8bits_1_sortiexor));
  Multiplexer #(.select(2), .width(8)) multiplexer_1 (
    .in0(add8bit_1_somme), .in1(or8bits_1_sortieor), .in2(and8bits_1_sortieand), .in3(xor8bits_1_sortiexor),
    .out(Resultat), .sel(ChoixOperation));
endmodule

module Etape4 (
  input  Rin,
  input  [7:0] A,
  input  [7:0] B,
  input  [1:0] ChoixOperation,
  output [7:0] Resultat
);

  UAL ual_1 (.Rin(Rin), .A(A), .B(B), .ChoixOperation(ChoixOperation), .Resultat(Resultat));
endmodule

module Registre8Bits (
  input  [7:0] Entree,
  input  Enable,
  output [7:0] Sortie
);

  wire Horloge_out;

  Register #(.width(1)) Bascule1 (.D(Entree[0]), .en(Enable), .clk(Horloge_out), .Q(Sortie[0]));  // open: clr
  Register #(.width(1)) Bascule2 (.D(Entree[1]), .en(Enable), .clk(Horloge_out), .Q(Sortie[1]));  // open: clr
  Register #(.width(1)) Bascule3 (.D(Entree[2]), .en(Enable), .clk(Horloge_out), .Q(Sortie[2]));  // open: clr
  Register #(.width(1)) Bascule4 (.D(Entree[3]), .en(Enable), .clk(Horloge_out), .Q(Sortie[3]));  // open: clr
  Clock Horloge (.out(Horloge_out));
  Register #(.width(1)) Bascule5 (.D(Entree[4]), .en(Enable), .clk(Horloge_out), .Q(Sortie[4]));  // open: clr
  Register #(.width(1)) Bascule6 (.D(Entree[5]), .en(Enable), .clk(Horloge_out), .Q(Sortie[5]));  // open: clr
  Register #(.width(1)) Bascule7 (.D(Entree[6]), .en(Enable), .clk(Horloge_out), .Q(Sortie[6]));  // open: clr
  Register #(.width(1)) Bascule8 (.D(Entree[7]), .en(Enable), .clk(Horloge_out), .Q(Sortie[7]));  // open: clr
endmodule

module BancDeRegistre (
  input  [7:0] Entree,
  input  Enable,
  input  [5:0] SelectionRegistre,
  output [7:0] A,
  output [7:0] B
);

  wire demultiplexer_1_out0, demultiplexer_1_out1, demultiplexer_1_out2, demultiplexer_1_out3;
  wire [7:0] R1_sortie, R2_sortie, R3_sortie, R4_sortie;

  Demultiplexer #(.select(2)) demultiplexer_1 (
    .out0(demultiplexer_1_out0), .out1(demultiplexer_1_out1), .out2(demultiplexer_1_out2),
    .out3(demultiplexer_1_out3), .in(Enable), .sel(SelectionRegistre[5:4]));
  Registre8Bits R1 (.Entree(Entree), .Enable(demultiplexer_1_out0), .Sortie(R1_sortie));
  Registre8Bits R2 (.Entree(Entree), .Enable(demultiplexer_1_out1), .Sortie(R2_sortie));
  Registre8Bits R3 (.Entree(Entree), .Enable(demultiplexer_1_out2), .Sortie(R3_sortie));
  Registre8Bits R4 (.Entree(Entree), .Enable(demultiplexer_1_out3), .Sortie(R4_sortie));
  Multiplexer #(.select(2), .width(8)) multiplexer_1 (
    .in0(R1_sortie), .in1(R2_sortie), .in2(R3_sortie), .in3(R4_sortie), .out(A), .sel(SelectionRegistre[3:2]));
  Multiplexer #(.select(2), .width(8)) multiplexer_2 (
    .in0(R1_sortie), .in1(R2_sortie), .in2(R3_sortie), .in3(R4_sortie), .out(B), .sel(SelectionRegistre[1:0]));
endmodule

module Etape5 (
  input  [7:0] Entree,
  input  Enable,
  input  [5:0] SelectionRegistre,
  output [7:0] A,
  output [7:0] B
);

  BancDeRegistre bancderegistre_1 (
    .Entree(Entree), .Enable(Enable), .SelectionRegistre(SelectionRegistre), .A(A), .B(B));
endmodule

module UniteTraitement (
  input  [7:0] Entree,
  input  Enable,
  input  [5:0] SelectionRegistre,
  input  [1:0] ChoixOperation,
  input  NewEntree,
  output [7:0] RegistreA,
  output [7:0] RegistreB
);

  wire [7:0] multiplexer_1_out, ual_1_resultat;

  Multiplexer #(.width(8)) multiplexer_1 (.in0(ual_1_resultat), .in1(Entree), .out(multiplexer_1_out), .sel(NewEntree));
  BancDeRegistre bancderegistre_1 (
    .Entree(multiplexer_1_out), .Enable(Enable), .SelectionRegistre(SelectionRegistre), .A(RegistreA),
    .B(RegistreB));
  UAL ual_1 (.A(RegistreA), .B(RegistreB), .ChoixOperation(ChoixOperation), .Resultat(ual_1_resultat));  // open: Rin
endmodule

module GestionDuPointeurProgramme (
  input  [7:0] Pas,
  input  Enable,
  output [7:0] PC
);

  wire [7:0] add8bit_1_somme;

  Registre8Bits registre8bits_1 (.Entree(add8bit_1_somme), .Enable(Enable), .Sortie(PC));
  Add8Bit add8bit_1 (.a(Pas), .b(PC), .Somme(add8bit_1_somme));  // open: Rin, Rout
endmodule

module Decodeur (
  input  [17:0] Instruction,
  output [1:0] Operation,
  output [5:0] Registres,
  output [7:0] Donnee,
  output Enable,
  output NewEntree
);


  assign Donnee = Instruction[15:8];
  assign Enable = Instruction[16];
  assign NewEntree = Instruction[17];
  assign Operation = Instruction[1:0];
  assign Registres = Instruction[7:2];
endmodule

module Etape7 (
  input  [7:0] Pas,
  input  Enable,
  output [7:0] RegADecimal,
  output [7:0] RegBDecimal
);

  wire decodeur_1_enable, decodeur_1_newentree;
  wire [1:0] decodeur_1_operation;
  wire [5:0] decodeur_1_registres;
  wire [7:0] decodeur_1_donnee, gestiondupointeurprogramme_1_pc;
  wire [17:0] rom_1_data;

  ROM #(.dataWidth(18)) rom_1 (.addr(gestiondupointeurprogramme_1_pc), .data(rom_1_data));
  GestionDuPointeurProgramme gestiondupointeurprogramme_1 (
    .Pas(Pas), .Enable(Enable), .PC(gestiondupointeurprogramme_1_pc));
  Decodeur decodeur_1 (
    .Instruction(rom_1_data), .Operation(decodeur_1_operation), .Registres(decodeur_1_registres),
    .Donnee(decodeur_1_donnee), .Enable(decodeur_1_enable), .NewEntree(decodeur_1_newentree));
  UniteTraitement unitetraitement_1 (
    .Entree(decodeur_1_donnee), .Enable(decodeur_1_enable), .SelectionRegistre(decodeur_1_registres),
    .ChoixOperation(decodeur_1_operation), .NewEntree(decodeur_1_newentree), .RegistreA(RegADecimal),
    .RegistreB(RegBDecimal));

  // Notes on the sheet:
  //   contents of rom_1 (hex, n*v repeats v):
  //   3045c 10004 10004 10004
endmodule

module Etape8 (
  input  [7:0] Pas,
  input  Enable,
  output [7:0] RegADecimal,
  output [7:0] RegBDecimal
);

  wire clock_1_out, decodeurv2_1_enable, decodeurv2_1_load, decodeurv2_1_newentree, decodeurv2_1_store;
  wire [1:0] decodeurv2_1_operation;
  wire [5:0] decodeurv2_1_registres;
  wire [7:0] decodeurv2_1_donnee, gestiondupointeurprogramme_1_pc, multiplexer_1_out, ram_1_dout;
  wire [19:0] rom_1_data;

  ROM #(.dataWidth(20)) rom_1 (.addr(gestiondupointeurprogramme_1_pc), .data(rom_1_data));
  GestionDuPointeurProgramme gestiondupointeurprogramme_1 (
    .Pas(Pas), .Enable(Enable), .PC(gestiondupointeurprogramme_1_pc));
  DecodeurV2 decodeurv2_1 (
    .Instruction(rom_1_data), .Operation(decodeurv2_1_operation), .Registres(decodeurv2_1_registres),
    .Donnee(decodeurv2_1_donnee), .Store(decodeurv2_1_store), .Load(decodeurv2_1_load),
    .Enable(decodeurv2_1_enable), .NewEntree(decodeurv2_1_newentree));
  Clock clock_1 (.out(clock_1_out));
  RAM #(.asyncread("true")) ram_1 (
    .addr(decodeurv2_1_donnee), .we(decodeurv2_1_store), .oe(decodeurv2_1_load), .clk(clock_1_out),
    .din(RegADecimal), .dout(ram_1_dout));
  Multiplexer #(.width(8)) multiplexer_1 (
    .in0(decodeurv2_1_donnee), .in1(ram_1_dout), .out(multiplexer_1_out), .sel(decodeurv2_1_load));
  UniteTraitement unitetraitement_1 (
    .Entree(multiplexer_1_out), .Enable(decodeurv2_1_enable), .SelectionRegistre(decodeurv2_1_registres),
    .ChoixOperation(decodeurv2_1_operation), .NewEntree(decodeurv2_1_newentree), .RegistreA(RegADecimal),
    .RegistreB(RegBDecimal));

  // Notes on the sheet:
  //   contents of rom_1 (hex, n*v repeats v):
  //   c045c 40004 40004 40004 1ff00 c0008 c2a5c 40004 40004 c0058 eff84 4000b
endmodule

module DecodeurV2 (
  input  [19:0] Instruction,
  output [1:0] Operation,
  output [5:0] Registres,
  output [7:0] Donnee,
  output Store,
  output Load,
  output Enable,
  output NewEntree
);


  assign Donnee = Instruction[15:8];
  assign Enable = Instruction[18];
  assign Load = Instruction[17];
  assign NewEntree = Instruction[19];
  assign Operation = Instruction[1:0];
  assign Registres = Instruction[7:2];
  assign Store = Instruction[16];
endmodule

module Etape9 (
  input  Enable,
  input  [7:0] Pas,
  output [7:0] RegADecimal,
  output [7:0] RegBDecimal
);

  wire clock_1_out, decodeurv3_1_enable, decodeurv3_1_jump, decodeurv3_1_load, decodeurv3_1_newentree,
       decodeurv3_1_store;
  wire [1:0] decodeurv3_1_operation;
  wire [5:0] decodeurv3_1_registres;
  wire [7:0] decodeurv3_1_donnee, gestiondupointeurprogramme_1_pc, multiplexer_1_out, multiplexer_2_out,
       ram_1_dout;
  wire [20:0] rom_1_data;

  ROM #(.dataWidth(21)) rom_1 (.addr(gestiondupointeurprogramme_1_pc), .data(rom_1_data));
  GestionDuPointeurProgramme gestiondupointeurprogramme_1 (
    .Pas(multiplexer_1_out), .Enable(Enable), .PC(gestiondupointeurprogramme_1_pc));
  Multiplexer #(.width(8)) multiplexer_1 (
    .in0(Pas), .in1(decodeurv3_1_donnee), .out(multiplexer_1_out), .sel(decodeurv3_1_jump));
  DecodeurV3 decodeurv3_1 (
    .Instruction(rom_1_data), .Jump(decodeurv3_1_jump), .Operation(decodeurv3_1_operation),
    .Registres(decodeurv3_1_registres), .Donnee(decodeurv3_1_donnee), .Store(decodeurv3_1_store),
    .Load(decodeurv3_1_load), .Enable(decodeurv3_1_enable), .NewEntree(decodeurv3_1_newentree));
  Clock clock_1 (.out(clock_1_out));
  RAM #(.asyncread("true")) ram_1 (
    .addr(decodeurv3_1_donnee), .we(decodeurv3_1_store), .oe(decodeurv3_1_load), .clk(clock_1_out),
    .din(RegADecimal), .dout(ram_1_dout));
  Multiplexer #(.width(8)) multiplexer_2 (
    .in0(decodeurv3_1_donnee), .in1(ram_1_dout), .out(multiplexer_2_out), .sel(decodeurv3_1_load));
  UniteTraitement unitetraitement_1 (
    .Entree(multiplexer_2_out), .Enable(decodeurv3_1_enable), .SelectionRegistre(decodeurv3_1_registres),
    .ChoixOperation(decodeurv3_1_operation), .NewEntree(decodeurv3_1_newentree), .RegistreA(RegADecimal),
    .RegistreB(RegBDecimal));

  // Notes on the sheet:
  //   contents of rom_1 (hex, n*v repeats v):
  //   1808b8 80008 80008 80008 3fe00 180010 1854b8 80008 80008 1800b0 1dff08 1401 9*0 80016
endmodule

module DecodeurV3 (
  input  [20:0] Instruction,
  output Jump,
  output [1:0] Operation,
  output [5:0] Registres,
  output [7:0] Donnee,
  output Store,
  output Load,
  output Enable,
  output NewEntree
);


  assign Donnee = Instruction[16:9];
  assign Enable = Instruction[19];
  assign Jump = Instruction[0];
  assign Load = Instruction[18];
  assign NewEntree = Instruction[20];
  assign Operation = Instruction[2:1];
  assign Registres = Instruction[8:3];
  assign Store = Instruction[17];
endmodule
